// Logisim project HALF ADDER.circ as structural Verilog: 1 circuit, main circuit main
module main (
  input  in_1,
  input  in_2,
  output out_3,
  output out_4
);

  ExactlyOne xor_1 (.out(out_3), .in0(in_1), .in1(in_1), .in2(in_1), .in3(in_1), .in4(in_2));
  and and_1 (out_4, in_2, in_1);
endmodule
