// Logisim project full substractor.circ as structural Verilog: 1 circuit, main circuit main
module main (
  input  in_1,
  input  in_2,
  output out_3,
  output out_4
);

  wire and_1_out, and_2_out, not_1_out, not_2_out, undriven, xor_1_out;

  not not_1 (not_1_out, in_1);
  ExactlyOne xor_1 (.out(xor_1_out), .in1(in_1), .in3(in_2), .in4(in_2));
  and and_1 (and_1_out, not_1_out, in_2);
  not not_2 (not_2_out, xor_1_out);
  xor xor_2 (out_3, xor_1_out, undriven);
  and and_2 (and_2_out, not_2_out, undriven, undriven);
  or or_1 (out_4, and_2_out, and_1_out, and_1_out);
endmodule
