// Logisim project two bit half subtractor.circ as structural Verilog: 1 circuit, main circuit main
module main (
  input  in_1,
  input  in_2,
  output out_3,
  output out_4
);

  wire not_1_out;

  not not_1 (not_1_out, in_1);
  ExactlyOne xor_1 (.out(out_3), .in1(in_1), .in2(in_1), .in3(in_1), .in4(in_1));
  and and_1 (out_4, not_1_out, not_1_out, not_1_out, in_1);

  assign in_2 = in_1;
endmodule
